# Fritzing sketch RPI-UV-Meter (saved by Fritzing 1.0.6)
breadboards: 1

parts:
  MCU1 = Raspberry Pi Zero [part_number=2W]
  Part1 = Adafruit VEML6075 UV Sensor Breakout [part_number=VEML6075]
  LCM1602_IIC1 = LCM1602 IIC [part_number="LCM1602 IIC V1" chip_label="LCM1602 IIC V1" package="DIP (Dual Inline) [THT]"]
  LCD1 = LCD screen [part_number="16x2 LCD" mpn=s mn=s]

nets:
  N1: MCU1.pin_1, Part1.3.3V
  N2: MCU1.pin_2, LCM1602_IIC1.VCC
  N3: MCU1.pin_3, Part1.SDA, LCM1602_IIC1.SDA
  N4: MCU1.pin_5, Part1.SCL, LCM1602_IIC1.SCL
  GND: MCU1.pin_9, Part1.GND, LCM1602_IIC1.GND
  VSS: LCM1602_IIC1.VSS, LCD1.VSS
  VDD: LCM1602_IIC1.VDD, LCD1.VDD
  N5: LCM1602_IIC1.V0, LCD1.V0
  N6: LCM1602_IIC1.RS, LCD1.RS
  N7: LCM1602_IIC1.RW, LCD1.R/W
  N8: LCM1602_IIC1.E, LCD1.E
  N9: LCM1602_IIC1.D0, LCD1.DB0
  N10: LCM1602_IIC1.D1, LCD1.DB1
  N11: LCM1602_IIC1.D2, LCD1.DB2
  N12: LCM1602_IIC1.D3, LCD1.DB3
  N13: LCM1602_IIC1.D4, LCD1.DB4
  N14: LCM1602_IIC1.D5, LCD1.DB5
  N15: LCM1602_IIC1.D6, LCD1.DB6
  N16: LCM1602_IIC1.D7, LCD1.DB7
  N17: LCM1602_IIC1.A, LCD1.LED+
  N18: LCM1602_IIC1.K, LCD1.LED-

custom parts:
  Adafruit VEML6075 UV Sensor Breakout: This little sensor is a great way to add UVA and UVB light sensing to any microcontroller project. The VEML6075 from Vishay has both true UVA and UVB band light sensors and an I2C-controlled ADC that will take readings and integrate them. The sensor also comes with calibration registers so you can easily convert the UVA/UVB readings into the UV Index. Compared to our other UV sensors, this one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
  LCM1602 IIC: I2C-Module to use a 1602 or 2004 LCD on with the wire.h libory Serial LCD Modul
